// Logisim project ALULi.circ as structural Verilog: 2 circuits, main circuit ALU
module ALU (
  input  [15:0] x,
  input  zx,
  input  nx,
  input  f,
  input  [15:0] y,
  input  zy,
  input  ny,
  input  no,
  output [15:0] o,
  output zr,
  output ng
);

  wire or_1_out;
  wire [15:0] add16_1_o, and_1_out, multiplexer_1_out, multiplexer_2_out, multiplexer_3_out,
       multiplexer_4_out, multiplexer_5_out, not_1_out, not_2_out, not_3_out;

  Multiplexer #(.width(16)) multiplexer_1 (.in0(x), .in1({16{1'b0}}), .out(multiplexer_1_out), .sel(zx));
  assign not_1_out = ~multiplexer_1_out;  // NOT_Gate not_1, 16 bits wide
  Multiplexer #(.width(16)) multiplexer_2 (.in0(y), .in1({16{1'b0}}), .out(multiplexer_2_out), .sel(zy));
  assign not_2_out = ~multiplexer_2_out;  // NOT_Gate not_2, 16 bits wide
  Multiplexer #(.width(16)) multiplexer_3 (.in0(multiplexer_1_out), .in1(not_1_out), .out(multiplexer_3_out), .sel(nx));
  Multiplexer #(.width(16)) multiplexer_4 (.in0(multiplexer_2_out), .in1(not_2_out), .out(multiplexer_4_out), .sel(ny));
  assign and_1_out = multiplexer_3_out & multiplexer_4_out;  // AND_Gate and_1, 16 bits wide
  Add16 add16_1 (.a(multiplexer_3_out), .b(multiplexer_4_out), .o(add16_1_o));  // open: Co
  Multiplexer #(.width(16)) multiplexer_5 (.in0(and_1_out), .in1(add16_1_o), .out(multiplexer_5_out), .sel(f));
  assign not_3_out = ~multiplexer_5_out;  // NOT_Gate not_3, 16 bits wide
  Multiplexer #(.width(16)) multiplexer_6 (.in0(multiplexer_5_out), .in1(not_3_out), .out({ng, o[14:0]}), .sel(no));
  or or_1 (or_1_out, o[0], o[1], o[2], o[3], o[4], o[5], o[6], o[7], o[8], o[9], o[10], o[11], o[12], o[13], o[14], ng);
  not not_4 (zr, or_1_out);

  assign o[15] = ng;
endmodule

module ALUUI (
);

  wire alu_1_ng, alu_1_zr, flags_sw1, flags_sw2, flags_sw3, flags_sw4, flags_sw5, flags_sw6;
  wire [15:0] alu_1_o, xl_sw8, yl_sw8;

  DipSwitch xl (
    .sw1(xl_sw8[7]), .sw2(xl_sw8[6]), .sw3(xl_sw8[5]), .sw4(xl_sw8[4]), .sw5(xl_sw8[3]), .sw6(xl_sw8[2]),
    .sw7(xl_sw8[1]), .sw8(xl_sw8[0]));
  DipSwitch yl (
    .sw1(yl_sw8[7]), .sw2(yl_sw8[6]), .sw3(yl_sw8[5]), .sw4(yl_sw8[4]), .sw5(yl_sw8[3]), .sw6(yl_sw8[2]),
    .sw7(yl_sw8[1]), .sw8(yl_sw8[0]));
  DipSwitch flags (
    .sw1(flags_sw1), .sw2(flags_sw2), .sw3(flags_sw3), .sw4(flags_sw4), .sw5(flags_sw5), .sw6(flags_sw6),
    .sw7(xl_sw8[15]), .sw8(yl_sw8[15]));
  LedBar ou (
    .led0(alu_1_o[15]), .led1(alu_1_o[14]), .led2(alu_1_o[13]), .led3(alu_1_o[12]), .led4(alu_1_o[11]),
    .led5(alu_1_o[10]), .led6(alu_1_o[9]), .led7(alu_1_o[8]));
  ALU alu_1 (
    .x(xl_sw8), .zx(flags_sw1), .nx(flags_sw2), .f(flags_sw3), .y(yl_sw8), .zy(flags_sw4), .ny(flags_sw5),
    .no(flags_sw6), .o(alu_1_o), .zr(alu_1_zr), .ng(alu_1_ng));
  LedBar ol (
    .led0(alu_1_o[7]), .led1(alu_1_o[6]), .led2(alu_1_o[5]), .led3(alu_1_o[4]), .led4(alu_1_o[3]),
    .led5(alu_1_o[2]), .led6(alu_1_o[1]), .led7(alu_1_o[0]));
  LED led_1 (.in(alu_1_zr));
  LED led_2 (.in(alu_1_ng));
endmodule
