// Logisim project Add16Lib.circ as structural Verilog: 2 circuits, main circuit Add16
module Add16 (
  input  [15:0] a,
  input  [15:0] b,
  output [15:0] o,
  output Co
);

  wire fulladder_1_carry, fulladder_2_carry, fulladder_3_carry, fulladder_4_carry, fulladder_5_carry,
       fulladder_6_carry, fulladder_7_carry, fulladder_8_carry, fulladder_9_carry, fulladder_10_carry,
       fulladder_11_carry, fulladder_12_carry, fulladder_13_carry, fulladder_14_carry, fulladder_15_carry;

  FullAdder fulladder_1 (.a(a[0]), .b(b[0]), .sum(o[0]), .carry(fulladder_1_carry));  // open: c
  FullAdder fulladder_2 (.a(a[1]), .b(b[1]), .c(fulladder_1_carry), .sum(o[1]), .carry(fulladder_2_carry));
  FullAdder fulladder_3 (.a(a[2]), .b(b[2]), .c(fulladder_2_carry), .sum(o[2]), .carry(fulladder_3_carry));
  FullAdder fulladder_4 (.a(a[3]), .b(b[3]), .c(fulladder_3_carry), .sum(o[3]), .carry(fulladder_4_carry));
  FullAdder fulladder_5 (.a(a[4]), .b(b[4]), .c(fulladder_4_carry), .sum(o[4]), .carry(fulladder_5_carry));
  FullAdder fulladder_6 (.a(a[5]), .b(b[5]), .c(fulladder_5_carry), .sum(o[5]), .carry(fulladder_6_carry));
  FullAdder fulladder_7 (.a(a[6]), .b(b[6]), .c(fulladder_6_carry), .sum(o[6]), .carry(fulladder_7_carry));
  FullAdder fulladder_8 (.a(a[7]), .b(b[7]), .c(fulladder_7_carry), .sum(o[7]), .carry(fulladder_8_carry));
  FullAdder fulladder_9 (.a(a[8]), .b(b[8]), .c(fulladder_8_carry), .sum(o[8]), .carry(fulladder_9_carry));
  FullAdder fulladder_10 (.a(a[9]), .b(b[9]), .c(fulladder_9_carry), .sum(o[9]), .carry(fulladder_10_carry));
  FullAdder fulladder_11 (.a(a[10]), .b(b[10]), .c(fulladder_10_carry), .sum(o[10]), .carry(fulladder_11_carry));
  FullAdder fulladder_12 (.a(a[11]), .b(b[11]), .c(fulladder_11_carry), .sum(o[11]), .carry(fulladder_12_carry));
  FullAdder fulladder_13 (.a(a[12]), .b(b[12]), .c(fulladder_12_carry), .sum(o[12]), .carry(fulladder_13_carry));
  FullAdder fulladder_14 (.a(a[13]), .b(b[13]), .c(fulladder_13_carry), .sum(o[13]), .carry(fulladder_14_carry));
  FullAdder fulladder_15 (.a(a[14]), .b(b[14]), .c(fulladder_14_carry), .sum(o[14]), .carry(fulladder_15_carry));
  FullAdder fulladder_16 (.a(a[15]), .b(b[15]), .c(fulladder_15_carry), .sum(o[15]), .carry(Co));
endmodule

module Add16UI (
);

  wire add16_1_co;
  wire [15:0] a_sw16, add16_1_o, b_sw16;

  DipSwitch #(.number(16)) a (
    .sw1(a_sw16[15]), .sw2(a_sw16[14]), .sw3(a_sw16[13]), .sw4(a_sw16[12]), .sw5(a_sw16[11]),
    .sw6(a_sw16[10]), .sw7(a_sw16[9]), .sw8(a_sw16[8]), .sw9(a_sw16[7]), .sw10(a_sw16[6]), .sw11(a_sw16[5]),
    .sw12(a_sw16[4]), .sw13(a_sw16[3]), .sw14(a_sw16[2]), .sw15(a_sw16[1]), .sw16(a_sw16[0]));
  DipSwitch #(.number(16)) b (
    .sw1(b_sw16[15]), .sw2(b_sw16[14]), .sw3(b_sw16[13]), .sw4(b_sw16[12]), .sw5(b_sw16[11]),
    .sw6(b_sw16[10]), .sw7(b_sw16[9]), .sw8(b_sw16[8]), .sw9(b_sw16[7]), .sw10(b_sw16[6]), .sw11(b_sw16[5]),
    .sw12(b_sw16[4]), .sw13(b_sw16[3]), .sw14(b_sw16[2]), .sw15(b_sw16[1]), .sw16(b_sw16[0]));
  LedBar #(.matrixcols(16)) o (
    .led0(add16_1_o[15]), .led1(add16_1_o[14]), .led2(add16_1_o[13]), .led3(add16_1_o[12]),
    .led4(add16_1_o[11]), .led5(add16_1_o[10]), .led6(add16_1_o[9]), .led7(add16_1_o[8]),
    .led8(add16_1_o[7]), .led9(add16_1_o[6]), .led10(add16_1_o[5]), .led11(add16_1_o[4]),
    .led12(add16_1_o[3]), .led13(add16_1_o[2]), .led14(add16_1_o[1]), .led15(add16_1_o[0]));
  Add16 add16_1 (.a(a_sw16), .b(b_sw16), .o(add16_1_o), .Co(add16_1_co));
  LED Carry (.in(add16_1_co));
endmodule
