// Logisim project BitLib.circ as structural Verilog: 2 circuits, main circuit Bit
module Bit (
  input  D,
  input  clk,
  input  load,
  output Q
);

  wire multiplexer_1_out;

  Multiplexer multiplexer_1 (.in0(Q), .in1(D), .out(multiplexer_1_out), .sel(load));
  D_Flip_Flop d_ff_1 (.D(multiplexer_1_out), .clk(clk), .Q(Q), .preset(1'b0), .reset(1'b0));  // open: Qn
endmodule

module BitUI (
);

  wire bit_1_q, clock_1_out, dipswitch_1_p1, dipswitch_1_p2;

  // DipSwitch #(.number(2)) dipswitch_1: pin names not known; wires that end beside it: dipswitch_1_p1, dipswitch_1_p2
  Bit bit_1 (.D(dipswitch_1_p1), .load(dipswitch_1_p2), .clk(clock_1_out), .Q(bit_1_q));
  Clock clock_1 (.out(clock_1_out));
  LED led_1 (.in(bit_1_q));
endmodule
