// Logisim project CPULib.circ as structural Verilog: 9 circuits, main circuit CPU
module CPU (
  input  [15:0] ins,
  input  [15:0] inM,
  input  clk,
  input  reset,
  output [15:0] outM,
  output writeM,
  output [15:0] addressM,
  output [15:0] prgmCtr,
  output f,
  output [15:0] x,
  output [15:0] y
);

  wire aluammuxctl_1_o, aregloadctl_1_o, aregmuxctl_1_out_2, dregloadctl_1_o, ng, pcincctl_1_o,
       pcloadctl_1_o, zr;
  wire [15:0] multiplexer_1_out;

  ARegMuxCtl aregmuxctl_1 (.in_1(ins), .out_2(aregmuxctl_1_out_2));
  ARegLoadCtl aregloadctl_1 (.instln(ins), .o(aregloadctl_1_o));
  Multiplexer #(.width(16)) multiplexer_1 (.in0(ins), .in1(outM), .out(multiplexer_1_out), .sel(aregmuxctl_1_out_2));
  PcLoadCtl pcloadctl_1 (.ins(ins), .zr(zr), .ng(ng), .o(pcloadctl_1_o));
  PCIncCtl pcincctl_1 (.reset(reset), .pcload(pcloadctl_1_o), .o(pcincctl_1_o));
  DRegLoadCtl dregloadctl_1 (.instln(ins), .o(dregloadctl_1_o));
  Reg16 A (.load(aregloadctl_1_o), .clk(clk), .D(multiplexer_1_out), .Q(addressM));
  PC pc_1 (.Inc(pcincctl_1_o), .load(pcloadctl_1_o), .reset(reset), .clk(clk), .i(addressM), .O(prgmCtr));
  Reg16 D (.load(dregloadctl_1_o), .clk(clk), .D(outM), .Q(x));
  Multiplexer #(.width(16)) multiplexer_2 (.in0(addressM), .in1(inM), .out(y), .sel(aluammuxctl_1_o));
  ALUAMMuxCtl aluammuxctl_1 (.instln(ins), .o(aluammuxctl_1_o));
  ALU alu_1 (
    .x(x), .zx(ins[11]), .nx(ins[10]), .f(ins[7]), .y(y), .zy(ins[9]), .ny(ins[8]), .no(ins[6]), .o(outM),
    .zr(zr), .ng(ng));
  WriteMCtl writemctl_1 (.instln(ins), .o(writeM));

  assign f = ins[7];

  // Other names for the same wires on the sheet: clock = clk; outA[15:0] = addressM
endmodule

module ARegMuxCtl (
  input  [15:0] in_1,
  output out_2
);


  assign out_2 = in_1[15];
endmodule

module ARegLoadCtl (
  input  [15:0] instln,
  output o
);

  wire and_1_out, not_1_out;

  and and_1 (and_1_out, instln[5], instln[15]);
  not not_1 (not_1_out, instln[15]);
  or or_1 (o, and_1_out, not_1_out);

  // Notes on the sheet:
  //   ~i or (i & d1)
endmodule

module ALUAMMuxCtl (
  input  [15:0] instln,
  output o
);

  and and_1 (o, instln[12], instln[15]);

  // Notes on the sheet:
  //   i & a
endmodule

module DRegLoadCtl (
  input  [15:0] instln,
  output o
);

  and and_1 (o, instln[4], instln[15]);

  // Notes on the sheet:
  //   i & d2
endmodule

module WriteMCtl (
  input  [15:0] instln,
  output o
);

  and and_1 (o, instln[3], instln[15]);

  // Notes on the sheet:
  //   i & d3
endmodule

module PcLoadCtl (
  input  [15:0] ins,
  input  zr,
  input  ng,
  output o
);

  wire j_out, jeq_out, jge_out, jgt_out, jle_out, jlt_out, jne_out, or_1_out, or_2_out, or_3_out;

  or or_1 (or_1_out, zr, ~ng);  // OR_Gate
  and jgt (jgt_out, ~ins[2], ~ins[1], ins[0], ~zr, ~ng);  // AND_Gate
  and jeq (jeq_out, ~ins[2], ins[1], ~ins[0], zr);  // AND_Gate
  and jge (jge_out, ~ins[2], ins[1], ins[0], or_1_out);  // AND_Gate
  and jlt (jlt_out, ins[2], ~ins[1], ~ins[0], ~zr, ng);  // AND_Gate
  and jne (jne_out, ins[2], ~ins[1], ins[0], ~zr);  // AND_Gate
  or or_2 (or_2_out, zr, ng);
  and j (j_out, ins[2], ins[1], ins[0]);
  and jle (jle_out, ins[2], ins[1], ~ins[0], or_2_out);  // AND_Gate
  or or_3 (or_3_out, jgt_out, jeq_out, jne_out, jge_out, jle_out, jlt_out, j_out);
  and and_1 (o, or_3_out, ins[15]);

  // Other names for the same wires on the sheet: j3 = ins[0]; j2 = ins[1]; j1 = ins[2]; i = ins[15]
endmodule

module PCIncCtl (
  input  reset,
  input  pcload,
  output o
);

  and and_1 (o, ~reset, ~pcload);  // AND_Gate
endmodule

module CPUUI (
);

  wire clk, cpu_1_f, cpu_1_writem, dipswitch_1_sw7;
  wire [13:0] cpu_1_addressm;
  wire [15:0] cpu_1_outm, cpu_1_prgmctr, cpu_1_x, cpu_1_y, ram_1_dout, rom_1_data;
  wire [15:14] cpu_1_addressm_2;

  ROM #(.addrWidth(15), .dataWidth(16)) rom_1 (.addr(cpu_1_prgmctr[14:0]), .data(rom_1_data));
  Clock u_clk (.out(clk));
  Button button_1 ();  // open: out
  DipSwitch dipswitch_1 (.sw7(dipswitch_1_sw7));  // open: sw1, sw2, sw3, sw4, sw5, sw6, sw8
  CPU cpu_1 (
    .ins(rom_1_data), .inM(ram_1_dout), .clk(clk), .reset(dipswitch_1_sw7), .outM(cpu_1_outm),
    .writeM(cpu_1_writem), .addressM({cpu_1_addressm_2, cpu_1_addressm}), .prgmCtr(cpu_1_prgmctr),
    .f(cpu_1_f), .x(cpu_1_x), .y(cpu_1_y));
  LED led_1 (.in(cpu_1_writem));
  LedBar #(.matrixcols(16)) ledbar_1 (
    .led0(cpu_1_addressm_2[15]), .led1(cpu_1_addressm_2[14]), .led2(cpu_1_addressm[13]),
    .led3(cpu_1_addressm[12]), .led4(cpu_1_addressm[11]), .led5(cpu_1_addressm[10]),
    .led6(cpu_1_addressm[9]), .led7(cpu_1_addressm[8]), .led8(cpu_1_addressm[7]), .led9(cpu_1_addressm[6]),
    .led10(cpu_1_addressm[5]), .led11(cpu_1_addressm[4]), .led12(cpu_1_addressm[3]),
    .led13(cpu_1_addressm[2]), .led14(cpu_1_addressm[1]), .led15(cpu_1_addressm[0]));
  LedBar #(.matrixcols(16)) ledbar_2 (
    .led0(cpu_1_prgmctr[15]), .led1(cpu_1_prgmctr[14]), .led2(cpu_1_prgmctr[13]), .led3(cpu_1_prgmctr[12]),
    .led4(cpu_1_prgmctr[11]), .led5(cpu_1_prgmctr[10]), .led6(cpu_1_prgmctr[9]), .led7(cpu_1_prgmctr[8]),
    .led8(cpu_1_prgmctr[7]), .led9(cpu_1_prgmctr[6]), .led10(cpu_1_prgmctr[5]), .led11(cpu_1_prgmctr[4]),
    .led12(cpu_1_prgmctr[3]), .led13(cpu_1_prgmctr[2]), .led14(cpu_1_prgmctr[1]), .led15(cpu_1_prgmctr[0]));
  LED f (.in(cpu_1_f));
  RAM #(.addrWidth(14), .dataWidth(16), .enables("line")) ram_1 (
    .addr(cpu_1_addressm), .we(cpu_1_writem), .clk(clk), .din(cpu_1_outm), .dout(ram_1_dout));
  LedBar #(.matrixcols(16)) ALUInputx (
    .led0(cpu_1_x[15]), .led1(cpu_1_x[14]), .led2(cpu_1_x[13]), .led3(cpu_1_x[12]), .led4(cpu_1_x[11]),
    .led5(cpu_1_x[10]), .led6(cpu_1_x[9]), .led7(cpu_1_x[8]), .led8(cpu_1_x[7]), .led9(cpu_1_x[6]),
    .led10(cpu_1_x[5]), .led11(cpu_1_x[4]), .led12(cpu_1_x[3]), .led13(cpu_1_x[2]), .led14(cpu_1_x[1]),
    .led15(cpu_1_x[0]));
  LedBar #(.matrixcols(16)) ALUInputy (
    .led0(cpu_1_y[15]), .led1(cpu_1_y[14]), .led2(cpu_1_y[13]), .led3(cpu_1_y[12]), .led4(cpu_1_y[11]),
    .led5(cpu_1_y[10]), .led6(cpu_1_y[9]), .led7(cpu_1_y[8]), .led8(cpu_1_y[7]), .led9(cpu_1_y[6]),
    .led10(cpu_1_y[5]), .led11(cpu_1_y[4]), .led12(cpu_1_y[3]), .led13(cpu_1_y[2]), .led14(cpu_1_y[1]),
    .led15(cpu_1_y[0]));
  LedBar #(.matrixcols(16)) ledbar_3 (
    .led0(cpu_1_outm[15]), .led1(cpu_1_outm[14]), .led2(cpu_1_outm[13]), .led3(cpu_1_outm[12]),
    .led4(cpu_1_outm[11]), .led5(cpu_1_outm[10]), .led6(cpu_1_outm[9]), .led7(cpu_1_outm[8]),
    .led8(cpu_1_outm[7]), .led9(cpu_1_outm[6]), .led10(cpu_1_outm[5]), .led11(cpu_1_outm[4]),
    .led12(cpu_1_outm[3]), .led13(cpu_1_outm[2]), .led14(cpu_1_outm[1]), .led15(cpu_1_outm[0]));

  // Notes on the sheet:
  //   contents of rom_1 (hex, n*v repeats v):
  //   0 fc10 1 f4d0 a e301 1 fc10 c ea87 0 fc10 2 e308 e ea87
  //   address out to RAM
  //   program counter
  //   data out to RAM, D, A
endmodule
