// Logisim project CouterLib.circ as structural Verilog: 2 circuits, main circuit PCUI
module PCUI (
);

  wire clock_1_out, sw_l_p1, sw_l_p2, sw_l_p3;
  wire [15:0] pc_1_o, swc_swr_sw16;

  // DipSwitch #(.number(3)) sw_l: pin names not known; wires that end beside it: sw_l_p1, sw_l_p2, sw_l_p3
  Clock clock_1 (.out(clock_1_out));
  DipSwitch #(.number(16)) swc_swr (
    .sw1(swc_swr_sw16[15]), .sw2(swc_swr_sw16[14]), .sw3(swc_swr_sw16[13]), .sw4(swc_swr_sw16[12]),
    .sw5(swc_swr_sw16[11]), .sw6(swc_swr_sw16[10]), .sw7(swc_swr_sw16[9]), .sw8(swc_swr_sw16[8]),
    .sw9(swc_swr_sw16[7]), .sw10(swc_swr_sw16[6]), .sw11(swc_swr_sw16[5]), .sw12(swc_swr_sw16[4]),
    .sw13(swc_swr_sw16[3]), .sw14(swc_swr_sw16[2]), .sw15(swc_swr_sw16[1]), .sw16(swc_swr_sw16[0]));
  PC pc_1 (.Inc(sw_l_p1), .load(sw_l_p2), .reset(sw_l_p3), .clk(clock_1_out), .i(swc_swr_sw16), .O(pc_1_o));
  LedBar #(.matrixcols(16)) o (
    .led0(pc_1_o[15]), .led1(pc_1_o[14]), .led2(pc_1_o[13]), .led3(pc_1_o[12]), .led4(pc_1_o[11]),
    .led5(pc_1_o[10]), .led6(pc_1_o[9]), .led7(pc_1_o[8]), .led8(pc_1_o[7]), .led9(pc_1_o[6]),
    .led10(pc_1_o[5]), .led11(pc_1_o[4]), .led12(pc_1_o[3]), .led13(pc_1_o[2]), .led14(pc_1_o[1]),
    .led15(pc_1_o[0]));
endmodule

module PC (
  input  Inc,
  input  load,
  input  reset,
  input  clk,
  input  [15:0] i,
  output [15:0] O
);

  wire inc16_1_co, or_1_out;
  wire [15:0] inc16_1_o, multiplexer_1_out, multiplexer_2_out, multiplexer_3_out;

  Multiplexer #(.width(16)) multiplexer_1 (.in1(inc16_1_o), .out(multiplexer_1_out), .sel(Inc));  // open: in0
  Multiplexer #(.width(16)) multiplexer_2 (.in0(multiplexer_1_out), .in1(i), .out(multiplexer_2_out), .sel(load));
  Multiplexer #(.width(16)) multiplexer_3 (
    .in0(multiplexer_2_out), .in1({16{1'b0}}), .out(multiplexer_3_out), .sel(reset));
  or or_1 (or_1_out, load, Inc, reset);
  Reg16 reg16_1 (.load(or_1_out), .clk(clk), .D(multiplexer_3_out), .Q(O));
  Inc16 inc16_1 (.a(O), .o(inc16_1_o), .Co(inc16_1_co));
  // NoConnect on inc16_1_co
endmodule
