// Logisim project FullAdderlib.circ as structural Verilog: 2 circuits, main circuit FullAdderUI
module FullAdderUI (
);

  wire abc_p1, abc_p2, abc_p3, fulladder_1_carry, fulladder_1_sum;

  // DipSwitch #(.number(3)) abc: pin names not known; wires that end beside it: abc_p1, abc_p2, abc_p3
  FullAdder fulladder_1 (.a(abc_p1), .b(abc_p2), .c(abc_p3), .sum(fulladder_1_sum), .carry(fulladder_1_carry));
  LED sum (.in(fulladder_1_sum));
  LED carry (.in(fulladder_1_carry));
endmodule

module FullAdder (
  input  a,
  input  b,
  input  c,
  output sum,
  output carry
);

  wire halfadder_1_carry, halfadder_1_sum, halfadder_2_carry;

  halfAdder halfadder_1 (.a(a), .b(b), .sum(halfadder_1_sum), .carry(halfadder_1_carry));
  halfAdder halfadder_2 (.a(halfadder_1_sum), .b(c), .sum(sum), .carry(halfadder_2_carry));
  or or_1 (carry, halfadder_2_carry, halfadder_1_carry);
endmodule
