// Logisim project Inc16Lib.circ as structural Verilog: 2 circuits, main circuit Inc16UI
module Inc16UI (
);

  wire inc16_1_co;
  wire [15:0] a_sw16, inc16_1_o;

  DipSwitch #(.number(16)) a (
    .sw1(a_sw16[15]), .sw2(a_sw16[14]), .sw3(a_sw16[13]), .sw4(a_sw16[12]), .sw5(a_sw16[11]),
    .sw6(a_sw16[10]), .sw7(a_sw16[9]), .sw8(a_sw16[8]), .sw9(a_sw16[7]), .sw10(a_sw16[6]), .sw11(a_sw16[5]),
    .sw12(a_sw16[4]), .sw13(a_sw16[3]), .sw14(a_sw16[2]), .sw15(a_sw16[1]), .sw16(a_sw16[0]));
  Inc16 inc16_1 (.a(a_sw16), .o(inc16_1_o), .Co(inc16_1_co));
  LED Co (.in(inc16_1_co));
  LedBar #(.matrixcols(16)) o (
    .led0(inc16_1_o[15]), .led1(inc16_1_o[14]), .led2(inc16_1_o[13]), .led3(inc16_1_o[12]),
    .led4(inc16_1_o[11]), .led5(inc16_1_o[10]), .led6(inc16_1_o[9]), .led7(inc16_1_o[8]),
    .led8(inc16_1_o[7]), .led9(inc16_1_o[6]), .led10(inc16_1_o[5]), .led11(inc16_1_o[4]),
    .led12(inc16_1_o[3]), .led13(inc16_1_o[2]), .led14(inc16_1_o[1]), .led15(inc16_1_o[0]));
endmodule

module Inc16 (
  input  [15:0] a,
  output [15:0] o,
  output Co
);

  Add16 add16_1 (.a(a), .b(16'h1), .o(o), .Co(Co));
endmodule
