// Logisim project RAM16KLib.circ as structural Verilog: 2 circuits, main circuit RAM16K
module RAM16K (
  input  load,
  input  clk,
  input  [15:0] Din,
  input  [13:0] Ain,
  output [15:0] Dout
);

  RAM #(.addrWidth(14), .dataWidth(16), .enables("line")) ram_1 (
    .addr(Ain), .we(load), .clk(clk), .din(Din), .dout(Dout));
endmodule

module RAM16KUI (
);

  wire button_1_out, clock_1_out;
  wire [13:0] dipswitch_2_sw14;
  wire [15:0] dipswitch_1_sw16, ram16k_1_dout;

  DipSwitch #(.number(16)) dipswitch_1 (
    .sw1(dipswitch_1_sw16[15]), .sw2(dipswitch_1_sw16[14]), .sw3(dipswitch_1_sw16[13]),
    .sw4(dipswitch_1_sw16[12]), .sw5(dipswitch_1_sw16[11]), .sw6(dipswitch_1_sw16[10]),
    .sw7(dipswitch_1_sw16[9]), .sw8(dipswitch_1_sw16[8]), .sw9(dipswitch_1_sw16[7]),
    .sw10(dipswitch_1_sw16[6]), .sw11(dipswitch_1_sw16[5]), .sw12(dipswitch_1_sw16[4]),
    .sw13(dipswitch_1_sw16[3]), .sw14(dipswitch_1_sw16[2]), .sw15(dipswitch_1_sw16[1]),
    .sw16(dipswitch_1_sw16[0]));
  DipSwitch #(.number(14)) dipswitch_2 (
    .sw1(dipswitch_2_sw14[13]), .sw2(dipswitch_2_sw14[12]), .sw3(dipswitch_2_sw14[11]),
    .sw4(dipswitch_2_sw14[10]), .sw5(dipswitch_2_sw14[9]), .sw6(dipswitch_2_sw14[8]),
    .sw7(dipswitch_2_sw14[7]), .sw8(dipswitch_2_sw14[6]), .sw9(dipswitch_2_sw14[5]),
    .sw10(dipswitch_2_sw14[4]), .sw11(dipswitch_2_sw14[3]), .sw12(dipswitch_2_sw14[2]),
    .sw13(dipswitch_2_sw14[1]), .sw14(dipswitch_2_sw14[0]));
  Button button_1 (.out(button_1_out));
  Clock clock_1 (.out(clock_1_out));
  RAM16K ram16k_1 (
    .load(button_1_out), .clk(clock_1_out), .Din(dipswitch_1_sw16), .Ain(dipswitch_2_sw14),
    .Dout(ram16k_1_dout));
  LedBar #(.matrixcols(16)) ledbar_1 (
    .led0(ram16k_1_dout[15]), .led1(ram16k_1_dout[14]), .led2(ram16k_1_dout[13]), .led3(ram16k_1_dout[12]),
    .led4(ram16k_1_dout[11]), .led5(ram16k_1_dout[10]), .led6(ram16k_1_dout[9]), .led7(ram16k_1_dout[8]),
    .led8(ram16k_1_dout[7]), .led9(ram16k_1_dout[6]), .led10(ram16k_1_dout[5]), .led11(ram16k_1_dout[4]),
    .led12(ram16k_1_dout[3]), .led13(ram16k_1_dout[2]), .led14(ram16k_1_dout[1]), .led15(ram16k_1_dout[0]));
endmodule
