// Logisim project RAMLib.circ as structural Verilog: 6 circuits, main circuit RAM8UI
module RAM8UI (
);

  wire clock_1_out, dipswitch_1_p1;
  wire [2:0] undriven;
  wire [15:0] ram8_1_q, swc_swr_sw16;

  DipSwitch #(.number(16)) swc_swr (
    .sw1(swc_swr_sw16[15]), .sw2(swc_swr_sw16[14]), .sw3(swc_swr_sw16[13]), .sw4(swc_swr_sw16[12]),
    .sw5(swc_swr_sw16[11]), .sw6(swc_swr_sw16[10]), .sw7(swc_swr_sw16[9]), .sw8(swc_swr_sw16[8]),
    .sw9(swc_swr_sw16[7]), .sw10(swc_swr_sw16[6]), .sw11(swc_swr_sw16[5]), .sw12(swc_swr_sw16[4]),
    .sw13(swc_swr_sw16[3]), .sw14(swc_swr_sw16[2]), .sw15(swc_swr_sw16[1]), .sw16(swc_swr_sw16[0]));
  // DipSwitch #(.number(4)) dipswitch_1: pin names not known; wires that end beside it: dipswitch_1_p1
  Clock clock_1 (.out(clock_1_out));
  RAM8 ram8_1 (.clk(clock_1_out), .load(dipswitch_1_p1), .Ain(undriven), .D(swc_swr_sw16), .Q(ram8_1_q));
  LedBar #(.matrixcols(16)) ledbar_1 (
    .led0(ram8_1_q[15]), .led1(ram8_1_q[14]), .led2(ram8_1_q[13]), .led3(ram8_1_q[12]), .led4(ram8_1_q[11]),
    .led5(ram8_1_q[10]), .led6(ram8_1_q[9]), .led7(ram8_1_q[8]), .led8(ram8_1_q[7]), .led9(ram8_1_q[6]),
    .led10(ram8_1_q[5]), .led11(ram8_1_q[4]), .led12(ram8_1_q[3]), .led13(ram8_1_q[2]), .led14(ram8_1_q[1]),
    .led15(ram8_1_q[0]));
endmodule

module RAM8 (
  input  clk,
  input  load,
  input  [2:0] Ain,
  input  [15:0] D,
  output [15:0] Q
);

  wire demultiplexer_1_out0, demultiplexer_1_out1, demultiplexer_1_out2, demultiplexer_1_out3,
       demultiplexer_1_out4, demultiplexer_1_out5, demultiplexer_1_out6, demultiplexer_1_out7;
  wire [15:0] reg16_1_q, reg16_2_q, reg16_3_q, reg16_4_q, reg16_5_q, reg16_6_q, reg16_7_q, reg16_8_q;

  Demultiplexer #(.select(3)) demultiplexer_1 (
    .out0(demultiplexer_1_out0), .out1(demultiplexer_1_out1), .out2(demultiplexer_1_out2),
    .out3(demultiplexer_1_out3), .out4(demultiplexer_1_out4), .out5(demultiplexer_1_out5),
    .out6(demultiplexer_1_out6), .out7(demultiplexer_1_out7), .in(load), .sel(Ain));
  Reg16 reg16_1 (.load(demultiplexer_1_out0), .clk(clk), .D(D), .Q(reg16_1_q));
  Reg16 reg16_2 (.load(demultiplexer_1_out1), .clk(clk), .D(D), .Q(reg16_2_q));
  Reg16 reg16_3 (.load(demultiplexer_1_out2), .clk(clk), .D(D), .Q(reg16_3_q));
  Reg16 reg16_4 (.load(demultiplexer_1_out3), .clk(clk), .D(D), .Q(reg16_4_q));
  Reg16 reg16_5 (.load(demultiplexer_1_out4), .clk(clk), .D(D), .Q(reg16_5_q));
  Reg16 reg16_6 (.load(demultiplexer_1_out5), .clk(clk), .D(D), .Q(reg16_6_q));
  Reg16 reg16_7 (.load(demultiplexer_1_out6), .clk(clk), .D(D), .Q(reg16_7_q));
  Reg16 reg16_8 (.load(demultiplexer_1_out7), .clk(clk), .D(D), .Q(reg16_8_q));
  Multiplexer #(.select(3), .width(16)) multiplexer_1 (
    .in0(reg16_1_q), .in1(reg16_2_q), .in2(reg16_3_q), .in3(reg16_4_q), .in4(reg16_5_q), .in5(reg16_6_q),
    .in6(reg16_7_q), .in7(reg16_8_q), .out(Q), .sel(Ain));
endmodule

module RAM64 (
  input  clk,
  input  load,
  input  [5:0] Ain,
  input  [15:0] D,
  output [15:0] Q
);

  wire demultiplexer_1_out0, demultiplexer_1_out1, demultiplexer_1_out2, demultiplexer_1_out3,
       demultiplexer_1_out4, demultiplexer_1_out5, demultiplexer_1_out6, demultiplexer_1_out7;
  wire [15:0] ram8_1_q, ram8_2_q, ram8_3_q, ram8_4_q, ram8_5_q, ram8_6_q, ram8_7_q, ram8_8_q;

  Demultiplexer #(.select(3)) demultiplexer_1 (
    .out0(demultiplexer_1_out0), .out1(demultiplexer_1_out1), .out2(demultiplexer_1_out2),
    .out3(demultiplexer_1_out3), .out4(demultiplexer_1_out4), .out5(demultiplexer_1_out5),
    .out6(demultiplexer_1_out6), .out7(demultiplexer_1_out7), .in(load), .sel(Ain[5:3]));
  RAM8 ram8_1 (.clk(clk), .load(demultiplexer_1_out0), .Ain(Ain[2:0]), .D(D), .Q(ram8_1_q));
  RAM8 ram8_2 (.clk(clk), .load(demultiplexer_1_out1), .Ain(Ain[2:0]), .D(D), .Q(ram8_2_q));
  RAM8 ram8_3 (.clk(clk), .load(demultiplexer_1_out2), .Ain(Ain[2:0]), .D(D), .Q(ram8_3_q));
  RAM8 ram8_4 (.clk(clk), .load(demultiplexer_1_out3), .Ain(Ain[2:0]), .D(D), .Q(ram8_4_q));
  RAM8 ram8_5 (.clk(clk), .load(demultiplexer_1_out4), .Ain(Ain[2:0]), .D(D), .Q(ram8_5_q));
  RAM8 ram8_6 (.clk(clk), .load(demultiplexer_1_out5), .Ain(Ain[2:0]), .D(D), .Q(ram8_6_q));
  RAM8 ram8_7 (.clk(clk), .load(demultiplexer_1_out6), .Ain(Ain[2:0]), .D(D), .Q(ram8_7_q));
  RAM8 ram8_8 (.clk(clk), .load(demultiplexer_1_out7), .Ain(Ain[2:0]), .D(D), .Q(ram8_8_q));
  Multiplexer #(.select(3), .width(16)) multiplexer_1 (
    .in0(ram8_1_q), .in1(ram8_2_q), .in2(ram8_3_q), .in3(ram8_4_q), .in4(ram8_5_q), .in5(ram8_6_q),
    .in6(ram8_7_q), .in7(ram8_8_q), .out(Q), .sel(Ain[5:3]));

  // Other names for the same wires on the sheet: Ain_t[2:0] = Ain[5:3]
endmodule

module RAM64UI (
);

  wire clock_1_out, dipswitch_1_p1;
  wire [5:0] undriven;
  wire [15:0] ram64_1_q, swc_swr_sw16;

  DipSwitch #(.number(16)) swc_swr (
    .sw1(swc_swr_sw16[15]), .sw2(swc_swr_sw16[14]), .sw3(swc_swr_sw16[13]), .sw4(swc_swr_sw16[12]),
    .sw5(swc_swr_sw16[11]), .sw6(swc_swr_sw16[10]), .sw7(swc_swr_sw16[9]), .sw8(swc_swr_sw16[8]),
    .sw9(swc_swr_sw16[7]), .sw10(swc_swr_sw16[6]), .sw11(swc_swr_sw16[5]), .sw12(swc_swr_sw16[4]),
    .sw13(swc_swr_sw16[3]), .sw14(swc_swr_sw16[2]), .sw15(swc_swr_sw16[1]), .sw16(swc_swr_sw16[0]));
  // DipSwitch #(.number(7)) dipswitch_1: pin names not known; wires that end beside it: dipswitch_1_p1
  Clock clock_1 (.out(clock_1_out));
  RAM64 ram64_1 (.clk(clock_1_out), .load(dipswitch_1_p1), .Ain(undriven), .D(swc_swr_sw16), .Q(ram64_1_q));
  LedBar #(.matrixcols(16)) ledbar_1 (
    .led0(ram64_1_q[15]), .led1(ram64_1_q[14]), .led2(ram64_1_q[13]), .led3(ram64_1_q[12]),
    .led4(ram64_1_q[11]), .led5(ram64_1_q[10]), .led6(ram64_1_q[9]), .led7(ram64_1_q[8]),
    .led8(ram64_1_q[7]), .led9(ram64_1_q[6]), .led10(ram64_1_q[5]), .led11(ram64_1_q[4]),
    .led12(ram64_1_q[3]), .led13(ram64_1_q[2]), .led14(ram64_1_q[1]), .led15(ram64_1_q[0]));
endmodule

module RAM512 (
  input  load,
  input  clk,
  input  [15:0] D,
  input  [8:0] Ain,
  output [15:0] Q
);

  wire demultiplexer_1_out0, demultiplexer_1_out1;
  wire [7:0] RAM_2_dout, RAM_4_dout;
  wire [15:8] RAM_1_dout, RAM_3_dout;

  Demultiplexer demultiplexer_1 (.out0(demultiplexer_1_out0), .out1(demultiplexer_1_out1), .in(load), .sel(Ain[8]));
  RAM #(.enables("line")) RAM_1 (
    .addr(Ain[7:0]), .we(demultiplexer_1_out0), .clk(clk), .din(D[15:8]), .dout(RAM_1_dout));
  RAM #(.enables("line")) RAM_3 (
    .addr(Ain[7:0]), .we(demultiplexer_1_out1), .clk(clk), .din(D[15:8]), .dout(RAM_3_dout));
  RAM #(.enables("line")) RAM_2 (
    .addr(Ain[7:0]), .we(demultiplexer_1_out0), .clk(clk), .din(D[7:0]), .dout(RAM_2_dout));
  RAM #(.enables("line")) RAM_4 (
    .addr(Ain[7:0]), .we(demultiplexer_1_out1), .clk(clk), .din(D[7:0]), .dout(RAM_4_dout));
  Multiplexer #(.width(16)) multiplexer_1 (
    .in0({RAM_1_dout, RAM_2_dout}), .in1({RAM_3_dout, RAM_4_dout}), .out(Q), .sel(Ain[8]));
endmodule

module RAM512UI (
);

  wire button_1_out, clock_1_out;
  wire [8:0] Ain_sw9;
  wire [15:0] ram512_1_q, swc_swr_sw16;

  DipSwitch #(.number(16)) swc_swr (
    .sw1(swc_swr_sw16[15]), .sw2(swc_swr_sw16[14]), .sw3(swc_swr_sw16[13]), .sw4(swc_swr_sw16[12]),
    .sw5(swc_swr_sw16[11]), .sw6(swc_swr_sw16[10]), .sw7(swc_swr_sw16[9]), .sw8(swc_swr_sw16[8]),
    .sw9(swc_swr_sw16[7]), .sw10(swc_swr_sw16[6]), .sw11(swc_swr_sw16[5]), .sw12(swc_swr_sw16[4]),
    .sw13(swc_swr_sw16[3]), .sw14(swc_swr_sw16[2]), .sw15(swc_swr_sw16[1]), .sw16(swc_swr_sw16[0]));
  DipSwitch #(.number(9)) Ain (
    .sw1(Ain_sw9[8]), .sw2(Ain_sw9[7]), .sw3(Ain_sw9[6]), .sw4(Ain_sw9[5]), .sw5(Ain_sw9[4]),
    .sw6(Ain_sw9[3]), .sw7(Ain_sw9[2]), .sw8(Ain_sw9[1]), .sw9(Ain_sw9[0]));
  Button button_1 (.out(button_1_out));
  Clock clock_1 (.out(clock_1_out));
  RAM512 ram512_1 (.load(button_1_out), .clk(clock_1_out), .D(swc_swr_sw16), .Ain(Ain_sw9), .Q(ram512_1_q));
  LedBar #(.matrixcols(16)) Q (
    .led0(ram512_1_q[15]), .led1(ram512_1_q[14]), .led2(ram512_1_q[13]), .led3(ram512_1_q[12]),
    .led4(ram512_1_q[11]), .led5(ram512_1_q[10]), .led6(ram512_1_q[9]), .led7(ram512_1_q[8]),
    .led8(ram512_1_q[7]), .led9(ram512_1_q[6]), .led10(ram512_1_q[5]), .led11(ram512_1_q[4]),
    .led12(ram512_1_q[3]), .led13(ram512_1_q[2]), .led14(ram512_1_q[1]), .led15(ram512_1_q[0]));
endmodule
