// Logisim project RegisterLib.circ as structural Verilog: 2 circuits, main circuit RegisterUI
module RegisterUI (
);

  wire clock_1_out, sw_l_p1;
  wire [15:0] reg16_1_q, swc_swr_sw16;

  DipSwitch #(.number(16)) swc_swr (
    .sw1(swc_swr_sw16[15]), .sw2(swc_swr_sw16[14]), .sw3(swc_swr_sw16[13]), .sw4(swc_swr_sw16[12]),
    .sw5(swc_swr_sw16[11]), .sw6(swc_swr_sw16[10]), .sw7(swc_swr_sw16[9]), .sw8(swc_swr_sw16[8]),
    .sw9(swc_swr_sw16[7]), .sw10(swc_swr_sw16[6]), .sw11(swc_swr_sw16[5]), .sw12(swc_swr_sw16[4]),
    .sw13(swc_swr_sw16[3]), .sw14(swc_swr_sw16[2]), .sw15(swc_swr_sw16[1]), .sw16(swc_swr_sw16[0]));
  // DipSwitch #(.number(2)) sw_l: pin names not known; wires that end beside it: sw_l_p1
  Clock clock_1 (.out(clock_1_out));
  Reg16 reg16_1 (.load(sw_l_p1), .clk(clock_1_out), .D(swc_swr_sw16), .Q(reg16_1_q));
  LedBar #(.matrixcols(16)) ledbar_1 (
    .led0(reg16_1_q[15]), .led1(reg16_1_q[14]), .led2(reg16_1_q[13]), .led3(reg16_1_q[12]),
    .led4(reg16_1_q[11]), .led5(reg16_1_q[10]), .led6(reg16_1_q[9]), .led7(reg16_1_q[8]),
    .led8(reg16_1_q[7]), .led9(reg16_1_q[6]), .led10(reg16_1_q[5]), .led11(reg16_1_q[4]),
    .led12(reg16_1_q[3]), .led13(reg16_1_q[2]), .led14(reg16_1_q[1]), .led15(reg16_1_q[0]));
endmodule

module Reg16 (
  input  load,
  input  clk,
  input  [15:0] D,
  output [15:0] Q
);

  Bit bit_1 (.D(D[0]), .load(load), .clk(clk), .Q(Q[0]));
  Bit bit_2 (.D(D[1]), .load(load), .clk(clk), .Q(Q[1]));
  Bit bit_3 (.D(D[2]), .load(load), .clk(clk), .Q(Q[2]));
  Bit bit_4 (.D(D[3]), .load(load), .clk(clk), .Q(Q[3]));
  Bit bit_5 (.D(D[4]), .load(load), .clk(clk), .Q(Q[4]));
  Bit bit_6 (.D(D[5]), .load(load), .clk(clk), .Q(Q[5]));
  Bit bit_7 (.D(D[6]), .load(load), .clk(clk), .Q(Q[6]));
  Bit bit_8 (.D(D[7]), .load(load), .clk(clk), .Q(Q[7]));
  Bit bit_9 (.D(D[8]), .load(load), .clk(clk), .Q(Q[8]));
  Bit bit_10 (.D(D[9]), .load(load), .clk(clk), .Q(Q[9]));
  Bit bit_11 (.D(D[10]), .load(load), .clk(clk), .Q(Q[10]));
  Bit bit_12 (.D(D[11]), .load(load), .clk(clk), .Q(Q[11]));
  Bit bit_13 (.D(D[12]), .load(load), .clk(clk), .Q(Q[12]));
  Bit bit_14 (.D(D[13]), .load(load), .clk(clk), .Q(Q[13]));
  Bit bit_15 (.D(D[14]), .load(load), .clk(clk), .Q(Q[14]));
  Bit bit_16 (.D(D[15]), .load(load), .clk(clk), .Q(Q[15]));
endmodule
